# Fritzing sketch touch_panel_1v (saved by Fritzing 0.9.3b)
circuit board: 7.098cm x 1.7cm
breadboards: 1

parts:
  C3 = Tantalum Capacitor [capacitance=10µF package="B 3528 [SMD, tantalum]"]
  C1 = Ceramic Capacitor [capacitance=100nF package="1206 [SMD, multilayer]"]
  R5 = Resistor [tolerance=±5% resistance=10k package="1206 [SMD]"]
  R4 = Resistor [tolerance=±5% resistance=6.8k package="1206 [SMD]"]
  R3 = Resistor [tolerance=±5% resistance=6.8k package="1206 [SMD]"]
  R2 = Resistor [tolerance=±5% resistance=6.8k package="1206 [SMD]"]
  R1 = Resistor [tolerance=±5% resistance=6.8k package="1206 [SMD]"]
  IC1 = SOIC-14 [chip_label=IC package=SO]
  Pad2 = Pad [width=17 height=14 connect=center]
  Pad1 = Pad [width=14 height=10 connect=center]
  Pad3 = Pad [width=17 height=14 connect=center]
  Pad4 = Pad [width=14 height=10 connect=center]
  J1 = male pin header, 5 pins [form="♂ (male)"]

nets:
  N1: C3.-, C1.1, IC1.2, IC1.14, J1.pin2
  N2: C3.+, C1.0, R5.Pin_1, IC1.1, J1.pin1
  N3: R5.Pin_0, IC1.4
  N4: R4.Pin_0, Pad3.pad
  N5: R4.Pin_1, IC1.13
  N6: R3.Pin_0, Pad4.pad
  N7: R3.Pin_1, IC1.12
  N8: R2.Pin_0, Pad2.pad
  N9: R2.Pin_1, IC1.11
  N10: R1.Pin_0, Pad1.pad
  N11: R1.Pin_1, IC1.10
  N12: IC1.3, J1.pin3
  N13: IC1.5, J1.pin4
  N14: IC1.6, J1.pin5

notes:
  Touch Panel v1
  Panel
  v1
  Tyro
  2017
  Touch
