# Fritzing sketch touch_panel_2v (saved by Fritzing 0.9.3b)
circuit board: 7.098cm x 3.6cm
breadboards: 1

parts:
  J1 = male pin header, 5 pins [form="♂ (male)"]
  IC1 = SOIC-14 [chip_label=IC package=SO]
  R1 = Resistor [tolerance=±5% resistance=10k package="1206 [SMD]"]
  R2 = Resistor [tolerance=±5% resistance=10k package="1206 [SMD]"]
  R3 = Resistor [tolerance=±5% resistance=10k package="1206 [SMD]"]
  R4 = Resistor [tolerance=±5% resistance=10k package="1206 [SMD]"]
  C1 = Ceramic Capacitor [capacitance=100nF package="1206 [SMD, multilayer]"]
  C3 = Tantalum Capacitor [capacitance=10µF package="B 3528 [SMD, tantalum]"]
  R6 = Resistor [tolerance=±5% resistance=47k package="1206 [SMD]"]
  R5 = Resistor [tolerance=±5% resistance=10k package="1206 [SMD]"]
  Pad4 = Pad [width=14 height=11 connect=center]
  Pad3 = Pad [width=17 height=15 connect=center]
  Pad1 = Pad [width=14 height=11 connect=center]
  Pad2 = Pad [width=17 height=15 connect=center]
  J2 = male pin header, 2 pins [form="♂ (male)"]
  J3 = male pin header, 2 pins [form="♂ (male)"]
  J5 = female pin header, 2 pins [form="♀ (female)"]
  J4 = female pin header, 2 pins [form="♀ (female)"]

nets:
  N1: J1.pin1, IC1.1, C1.0, C3.+, R6.Pin_1, R5.Pin_1
  N2: J1.pin2, IC1.2, IC1.14, C1.1, C3.-
  N3: J1.pin3, IC1.3
  N4: J1.pin4, IC1.5, R6.Pin_0
  N5: J1.pin5, IC1.6
  N6: IC1.4, R5.Pin_0
  N7: IC1.10, R1.Pin_1
  N8: IC1.11, R2.Pin_1
  N9: IC1.12, R3.Pin_1
  N10: IC1.13, R4.Pin_1
  N11: R1.Pin_0, J5.pin2
  N12: R2.Pin_0, J5.pin1
  N13: R3.Pin_0, J4.pin2
  N14: R4.Pin_0, J4.pin1
  N15: Pad4.pad, J2.pin1
  N16: Pad3.pad, J2.pin2
  N17: Pad1.pad, J3.pin2
  N18: Pad2.pad, J3.pin1

notes:
  Panel
  v2
  Tyro
  2017
  Touch
