# Fritzing sketch schema_v0.2 (saved by Fritzing 0.9.3b)
circuit board: 7.8cm x 7cm
breadboards: 1

parts:
  U1 = mystery part, 20 pins [chip_label=?]
  Part1 = BluePill  # not connected
  U2 = mystery part, 20 pins [chip_label=?]
  J1 = female pin header, 20 pins [form="♀ (female)"]
  U3 = mystery part, 40 pins [chip_label=?]
  R1 = Trimmer Potentiometer [maximum_resistance=10kΩ package=THT]
  J7 = female pin header, 5 pins [form="♀ (female)" part_number="RTC connection"]
  R2 = Resistor [tolerance=±5% resistance=180 package=THT]
  J9 = female pin header, 5 pins [form="♀ (female)" part_number="Buttons connector"]
  J8 = female pin header, 4 pins [form="♀ (female)" part_number="BMS pajungimas"]

nets:
  N1: U1.pin1, U2.pin1, J1.pin3, J1.pin20, U3.pin19, R1.leg1, J7.pin5, J9.pin5, J8.pin1
  N2: U1.pin2, J1.pin1
  N3: U1.pin3, J1.pin2
  N4: U1.pin4, J1.pin6
  N5: U1.pin5, J1.pin7
  N6: U1.pin6, J1.pin8
  N7: U1.pin7, J1.pin9
  N8: U1.pin8, J1.pin10
  N9: U1.pin9, J1.pin11
  N10: U1.pin10, U2.pin10, J1.pin4, J1.pin17, U3.pin18, R1.leg2, J8.pin4
  N11: U1.pin11, U1.pin20, U2.pin11, U2.pin20, U3.pin38
  N12: U1.pin12, U3.pin29
  N13: U1.pin13, U3.pin28
  N14: U1.pin14, U3.pin27
  N15: U1.pin15, U3.pin26
  N16: U1.pin16, U3.pin25
  N17: U1.pin17, U3.pin24
  N18: U1.pin18, U3.pin16
  N19: U1.pin19, U3.pin17
  N20: U2.pin2, J1.pin12
  N21: U2.pin3, J1.pin13
  N22: U2.pin4, J1.pin14
  N23: U2.pin5, J1.pin15
  N24: U2.pin6, J1.pin16
  N25: U2.pin15, U3.pin34
  N26: U2.pin16, U3.pin33
  N27: U2.pin17, U3.pin32
  N28: U2.pin18, U3.pin31
  N29: U2.pin19, U3.pin30
  N30: J1.pin18, R1.wiper
  N31: J1.pin19, R2.Pin_0
  N32: U3.pin5, R2.Pin_1
  N33: U3.pin6, J8.pin2
  N34: U3.pin7, J8.pin3
  N35: U3.pin8, J9.pin1
  N36: U3.pin9, J9.pin2
  N37: U3.pin10, J9.pin3
  N38: U3.pin11, J9.pin4
  N39: U3.pin14, J7.pin3
  N40: U3.pin15, J7.pin2
  N41: U3.pin20, J7.pin1

notes:
  TinyBMS
  Display v1
  Tyro 2018-03
  BMS
  +
  -
  buttons
  RTC
