# Fritzing sketch schema_v0.3 (saved by Fritzing 0.9.3b)
breadboards: 1

parts:
  J7 = female pin header, 5 pins [form="♀ (female)" part_number="RTC connection"]
  R2 = Resistor [tolerance=±5% resistance=180 package=THT]
  J2 = female pin header, 5 pins [form="♀ (female)" part_number="touch shiel connection"]
  U1 = mystery part, 20 pins [chip_label=?]
  Part1 = BluePill
  J1 = female pin header, 20 pins [form="♀ (female)"]
  J8 = female pin header, 4 pins [form="♀ (female)" part_number="BMS pajungimas"]
  U2 = mystery part, 20 pins [chip_label=?]
  R1 = Trimmer Potentiometer [maximum_resistance=10kΩ package=THT]

nets:
  N1: J7.pin1, J2.pin1, Part1.3V31
  N2: J7.pin2, J2.pin3, Part1.B7
  N3: J7.pin3, J2.pin4, Part1.B6
  N4: J7.pin5, J2.pin2, U1.pin1, Part1.GND3, J1.pin3, J1.pin20, J8.pin1, U2.pin1, R1.leg1
  N5: R2.Pin_0, J1.pin19
  N6: R2.Pin_1, Part1.A8
  N7: J2.pin5, Part1.B4
  N8: U1.pin2, J1.pin1
  N9: U1.pin3, J1.pin2
  N10: U1.pin4, J1.pin6
  N11: U1.pin5, J1.pin7
  N12: U1.pin6, J1.pin8
  N13: U1.pin7, J1.pin9
  N14: U1.pin8, J1.pin10
  N15: U1.pin9, J1.pin11
  N16: U1.pin10, Part1.5V, J1.pin4, J1.pin17, J8.pin4, U2.pin10, R1.leg2
  N17: U1.pin11, U1.pin20, Part1.3V3, U2.pin11, U2.pin20
  N18: U1.pin12, Part1.A4
  N19: U1.pin13, Part1.A5
  N20: U1.pin14, Part1.A6
  N21: U1.pin15, Part1.A7
  N22: U1.pin16, Part1.B0
  N23: U1.pin17, Part1.B1
  N24: U1.pin18, Part1.B8
  N25: U1.pin19, Part1.B9
  N26: Part1.C15, U2.pin15
  N27: Part1.A0, U2.pin16
  N28: Part1.A1, U2.pin17
  N29: Part1.A3, U2.pin19
  N30: Part1.A10, J8.pin3
  N31: Part1.A9, J8.pin2
  N32: Part1.A2, U2.pin18
  N33: J1.pin12, U2.pin2
  N34: J1.pin13, U2.pin3
  N35: J1.pin14, U2.pin4
  N36: J1.pin15, U2.pin5
  N37: J1.pin16, U2.pin6
  N38: J1.pin18, R1.wiper
